// Logisim project Contador.circ as structural Verilog: 3 circuits, main circuit main
module main (
  input  PRESET,
  input  in_2,
  input  J,
  input  in_4,
  input  K,
  input  CLEAR,
  input  in_7,
  output out_8,
  output out_9,
  output out_10,
  output out_11,
  output out_12,
  output out_13,
  output out_14,
  output out_15,
  output out_16,
  output out_17
);

  wire and_1_out, and_2_out, clock_1_out, clock_2_out, clock_3_out, contador_up_down_1_salida_final_t,
       j_k_ff_1_q, j_k_ff_2_q, j_k_ff_3_q, j_k_ff_4_q, nand_1_out, nand_2_out, not_1_out, not_2_out;

  Clock clock_1 (.out(clock_1_out));
  nand nand_1 (nand_1_out, out_9, J, clock_1_out);
  nand nand_2 (nand_2_out, clock_1_out, K, out_8);
  not not_1 (not_1_out, PRESET);
  nand nand_3 (out_8, not_1_out, nand_1_out, out_9);
  nand nand_4 (out_9, out_8, nand_2_out, not_2_out);
  not not_2 (not_2_out, CLEAR);
  Clock clock_2 (.out(clock_2_out));
  Clock clock_3 (.out(clock_3_out));
  Contador_Up_down contador_up_down_1 (
    .in_1(in_7), .in_2(1'b1), .out_4(out_10), .out_5(out_11), .out_6(out_12), .out_7(out_13),
    .Salida_final_T(contador_up_down_1_salida_final_t));
  J_K_Flip_Flop j_k_ff_1 (.J(in_2), .clk(clock_3_out), .K(in_2), .Q(j_k_ff_1_q), .en(in_4));  // open: Qn, preset, reset
  and and_1 (and_1_out, j_k_ff_1_q, j_k_ff_2_q);
  J_K_Flip_Flop j_k_ff_2 (
    .J(j_k_ff_1_q), .clk(clock_3_out), .K(j_k_ff_1_q), .Q(j_k_ff_2_q), .en(in_4));  // open: Qn, preset, reset
  // Contador_Up_down contador_up_down_2: pin names not known; wires that end beside it: in_7, clock_2_out, contador_up_down_1_salida_final_t, out_14, out_15, out_16, out_17
  J_K_Flip_Flop j_k_ff_3 (
    .J(and_1_out), .clk(clock_3_out), .K(and_1_out), .Q(j_k_ff_3_q), .en(in_4));  // open: Qn, preset, reset
  and and_2 (and_2_out, and_1_out, j_k_ff_3_q);
  J_K_Flip_Flop j_k_ff_4 (
    .J(and_2_out), .clk(clock_3_out), .K(and_2_out), .Q(j_k_ff_4_q), .en(in_4));  // open: Qn, preset, reset

  // Notes on the sheet:
  //   CONTADOR DE 0 A 100 
  //   UP and Down
  //   CONTADOR
  //   DE 4 BITS
endmodule

module Contador_Decadas (
  input  in_1,
  input  in_2,
  output out_3,
  output out_4,
  output out_5,
  output out_6,
  output out_7
);

  wire and_1_out, and_2_out, and_3_out;

  J_K_Flip_Flop j_k_ff_1 (.J(1'b1), .clk(in_1), .K(1'b1), .Q(out_4), .en(in_2), .reset(and_2_out));  // open: Qn, preset
  J_K_Flip_Flop j_k_ff_2 (
    .J(out_4), .clk(in_1), .K(out_4), .Q(out_5), .en(in_2), .reset(and_2_out));  // open: Qn, preset
  and and_1 (and_1_out, out_4, out_5);
  and and_2 (and_2_out, out_5, out_7);
  J_K_Flip_Flop j_k_ff_3 (
    .J(and_1_out), .clk(in_1), .K(and_1_out), .Q(out_6), .en(in_2), .reset(and_2_out));  // open: Qn, preset
  and and_3 (and_3_out, and_1_out, out_6);
  J_K_Flip_Flop j_k_ff_4 (
    .J(and_3_out), .clk(in_1), .K(and_3_out), .Q(out_7), .en(in_2), .reset(and_2_out));  // open: Qn, preset
  and and_4 (out_3, out_7, out_4);

  // Notes on the sheet:
  //   CONTADOR DE DECADAS
endmodule

module Contador_Up_down (
  input  in_1,
  input  in_2,
  output Salida_final_T,
  output out_4,
  output out_5,
  output out_6,
  output out_7
);

  wire and_1_out, and_2_out, and_3_out, and_4_out, and_5_out, and_6_out, and_7_out, and_8_out, and_9_out,
       and_10_out, clock_1_out, j_k_ff_1_qn, j_k_ff_2_qn, j_k_ff_3_qn, not_1_out, not_2_out, not_3_out,
       not_4_out, not_5_out, not_6_out, not_7_out, not_8_out, not_9_out, or_1_out, or_2_out, or_3_out,
       or_4_out, or_5_out;

  Clock clock_1 (.out(clock_1_out));
  not not_1 (not_1_out, out_4);
  not not_2 (not_2_out, out_6);
  not not_3 (not_3_out, in_1);
  not not_4 (not_4_out, in_1);
  and and_1 (and_1_out, out_4, out_5, out_6, out_7, in_1);
  and and_2 (and_2_out, not_1_out, out_5, not_2_out, out_7, not_3_out);
  J_K_Flip_Flop j_k_ff_1 (
    .J(1'b1), .clk(clock_1_out), .K(1'b1), .Q(out_4), .Qn(j_k_ff_1_qn), .preset(and_1_out), .en(in_2),
    .reset(and_2_out));
  and and_3 (and_3_out, not_4_out, out_4);
  or or_1 (or_1_out, and_3_out, and_4_out);
  and and_4 (and_4_out, j_k_ff_1_qn, in_1);
  J_K_Flip_Flop j_k_ff_2 (
    .J(or_1_out), .clk(clock_1_out), .K(or_1_out), .Q(out_5), .Qn(j_k_ff_2_qn), .en(in_2), .reset(or_2_out));  // open: preset
  or or_2 (or_2_out, and_2_out, and_1_out);
  and and_5 (and_5_out, and_3_out, out_5);
  and and_6 (and_6_out, j_k_ff_2_qn, and_4_out);
  or or_3 (or_3_out, and_5_out, and_6_out);
  and and_7 (and_7_out, and_5_out, out_6);
  J_K_Flip_Flop j_k_ff_3 (
    .J(or_3_out), .clk(clock_1_out), .K(or_3_out), .Q(out_6), .Qn(j_k_ff_3_qn), .en(in_2), .reset(or_4_out));  // open: preset
  and and_8 (and_8_out, j_k_ff_3_qn, and_6_out);
  or or_4 (or_4_out, and_2_out, and_1_out);
  or or_5 (or_5_out, and_7_out, and_8_out);
  and and_9 (and_9_out, out_7, not_7_out, or_1_out);
  J_K_Flip_Flop j_k_ff_4 (
    .J(or_5_out), .clk(clock_1_out), .K(or_5_out), .Q(out_7), .preset(and_1_out), .en(in_2), .reset(and_2_out));  // open: Qn
  not not_5 (not_5_out, out_4);
  not not_6 (not_6_out, out_5);
  not not_7 (not_7_out, in_1);
  not not_8 (not_8_out, out_6);
  not not_9 (not_9_out, out_7);
  or or_6 (Salida_final_T, and_9_out, and_10_out);
  and and_10 (and_10_out, not_5_out, not_6_out, not_8_out, not_9_out, in_1);

  // Other names for the same wires on the sheet: _1 = out_4; _2 = out_5; _4 = out_6; _8 = out_7; UD = in_1

  // Notes on the sheet:
  //   Reset D
  //   Reset U
endmodule
